// Logisim project bienvenue.circ as structural Verilog: 6 circuits, main circuit main
module main (
);

  partie_1 partie_1_1 ();
  partie_2 partie_2_1 ();

  // Notes on the sheet:
  //   Partie 1 : 
  //   Partie 2 : 
  //   Partie 3 : 
  //   Partie 4 : 
  //   Bientôt le début :)
  //   Le composant que tu vois en dessous est en fait un autre circuit.
  //   Pour y accéder, double clique dessus avec l'outil qui ressemble à cela : 
  //   Tu peux accéder au circuit de la même manière que pour la partie 1.
  //   On va commencer à s'intéresser à des choses un peu plus concrètes...
  //   Pas vraiment de challenge ici, par contre le raccourci que j'avais mis ici a disparu...
endmodule

module partie_1 (
);


  // Notes on the sheet:
  //   Bravo, la première partie du flag est : 404CTF{L3_
  //   pour revenir dans le circuit principal, tu peux double cliquer sur "main" dans l'arborescence à gauche
  //   tu peux donc aussi procéder ainsi pour accéder à n'importe quel sous-circuit
  //   on m'a dit de mettre du comic sans, comme quoi ça faisait plus accueillant, pas mal, non ?
endmodule

module partie_2 (
);

  wire clock_1_out;
  wire [3:0] counter_1_q;
  wire [7:0] multiplexer_1_out;

  Counter #(.width(4), .max('hf)) counter_1 (.Q(counter_1_q), .clk(clock_1_out));  // open: load, D, count, carry, clr
  Clock clock_1 (.out(clock_1_out));
  Multiplexer #(.select(4), .width(8)) multiplexer_1 (
    .in0(8'h4d), .in1(8'h30), .in2(8'h6d), .in3(8'h33), .in4(8'h6e), .in5(8'h54), .in6(8'h5f), .in7(8'h33),
    .in8(8'h53), .in9(8'h74), .in10(8'h5f), .in11(8'h56), .in12(8'h33), .in13(8'h6e), .in14(8'h55),
    .in15(8'h5f), .out(multiplexer_1_out), .sel(counter_1_q));  // open: en
  Hex_Digit_Display hex_digit_display_1 (.value(multiplexer_1_out[3:0]));  // open: dp
  Hex_Digit_Display hex_digit_display_2 (.value(multiplexer_1_out[7:4]));  // open: dp

  // Notes on the sheet:
  //   bien, maintenant, intéressons nous aux multiplexers... Peut-être qu'intéragir avec la clock, pourrait te permettre d'en comprendre le fonctionnement ?
  //   Tu pourras rentrer le code obtenu dans la partie 3
  //   -> tu cherches ici une suite de bytes qui boucle,
  //   le début est 4d, la fin 5f.
endmodule

module partie_3 (
);

  wire clock_1_out;
  wire [3:0] counter_1_q;
  wire [6:0] rom_1_data;

  Clock clock_1 (.out(clock_1_out));
  Counter #(.width(4), .max('hf), .ongoal("stay"), .trigger("falling")) counter_1 (
    .Q(counter_1_q), .clk(clock_1_out));  // open: load, D, count, carry, clr
  ROM #(.addrWidth(4), .dataWidth(7)) rom_1 (.addr(counter_1_q), .data(rom_1_data));  // open: sel
  TTY #(.rows(1), .cols(16)) tty_1 (.data(rom_1_data), .clk(clock_1_out));  // open: we, clr

  // Notes on the sheet:
  //   Tu peux rentrer de l'hexadécimal dans la rom
  //   en cliquant dessus avec l'outil qui ressemble à cela :
  //   puis sur (click to edit) dans ses propriétés
  //   contents of rom_1 (hex, n*v repeats v):
  //   4d 30 6d 33 6e 54 5f 33 53 74 5f 56 33 6e 55 5f
  //   à la fin de l'affichage du flag, il n'y aura plus de place sur l'écran et la simulation va planter
  //   souviens-toi que tu pourras alors utiliser ctrl+r puis ctrl+e pour tout remettre en ordre
  //   et le texte correspondant s'affichera à l'écran
endmodule

module partie_4 (
);

  wire clock_1_out;
  wire [3:0] counter_1_q;
  wire [7:0] multiplexer_1_out, partie_4_blackbox_1_out_2;

  Counter #(.width(4), .max('hf)) counter_1 (.Q(counter_1_q), .clk(clock_1_out));  // open: load, D, count, carry, clr
  Clock clock_1 (.out(clock_1_out));
  Multiplexer #(.select(4), .width(8)) multiplexer_1 (
    .in0(8'h44), .in1(8'h33), .in2(8'h5f), .in3(8'h35), .in4(8'h34), .in5(8'h6d), .in6(8'h75), .in7(8'h73),
    .in8(8'h33), .in9(8'h72), .in10(8'h7d), .in11({8{1'b0}}), .in12({8{1'b0}}), .in13({8{1'b0}}),
    .in14({8{1'b0}}), .in15({8{1'b0}}), .out(multiplexer_1_out), .sel(counter_1_q));  // open: en
  partie_4_blackbox partie_4_blackbox_1 (.in_1(multiplexer_1_out), .out_2(partie_4_blackbox_1_out_2));
  Hex_Digit_Display hex_digit_display_1 (.value(partie_4_blackbox_1_out_2[7:4]));  // open: dp
  Hex_Digit_Display hex_digit_display_2 (.value(partie_4_blackbox_1_out_2[3:0]));  // open: dp

  // Notes on the sheet:
  //   Une des particularités du hardware, est que l'on peut modifier le circuit à notre guise...
endmodule

module partie_4_blackbox (
  input  [7:0] in_1,
  output [7:0] out_2
);

  wire clock_1_out;
  wire [3:0] counter_1_q;
  wire [6:0] rom_1_data;

  Clock clock_1 (.out(clock_1_out));
  Counter #(.width(4), .max('hf), .ongoal("stay"), .trigger("falling")) counter_1 (
    .Q(counter_1_q), .clk(clock_1_out));  // open: load, D, count, carry, clr
  assign out_2 = in_1 | 8'h1;  // OR_Gate or_1, 8 bits wide
  ROM #(.addrWidth(4), .dataWidth(7)) rom_1 (.addr(counter_1_q), .data(rom_1_data));  // open: sel
  TTY #(.rows(1), .cols(16)) tty_1 (.data(rom_1_data), .clk(clock_1_out));  // open: we, clr

  // Notes on the sheet:
  //   ...alors profites-en !
  //   contents of rom_1 (hex, n*v repeats v):
  //   44 33 5f 35 34 6d 75 73 33 72 7d
endmodule
