// Logisim project reveil.circ as structural Verilog: 2 circuits, main circuit main
module main (
  input  [31:0] Input
);

  wire clock_1_out;
  wire [2:0] counter_1_q;
  wire [15:0] multiplexer_1_out, multiplexer_2_out;
  wire [31:0] blackbox_1_output, rom_1_data, rom_2_data;

  Counter #(.width(3), .max('h7)) counter_1 (.Q(counter_1_q), .clk(clock_1_out));  // open: load, D, count, carry, clr
  Clock clock_1 (.out(clock_1_out));
  ROM #(.addrWidth(2), .dataWidth(32)) rom_1 (.addr(counter_1_q[1:0]), .data(rom_1_data));  // open: sel
  ROM #(.addrWidth(2), .dataWidth(32)) rom_2 (.addr(counter_1_q[1:0]), .data(rom_2_data));  // open: sel
  _7_Segment_Display u_7_segment_display_1 (
    .g(blackbox_1_output[31]), .f(blackbox_1_output[30]), .a(blackbox_1_output[29]),
    .b(blackbox_1_output[28]), .e(blackbox_1_output[27]), .d(blackbox_1_output[26]),
    .c(blackbox_1_output[25]), .dp(blackbox_1_output[24]));
  Multiplexer #(.select(3), .width(16)) multiplexer_1 (
    .in0(rom_2_data[15:0]), .in1(rom_2_data[31:16]), .in2(rom_2_data[31:16]), .in3(rom_2_data[15:0]),
    .in4(rom_2_data[31:16]), .in5(rom_1_data[31:16]), .in6(rom_1_data[31:16]), .in7(rom_2_data[31:16]),
    .out(multiplexer_1_out), .sel(counter_1_q));  // open: en
  _7_Segment_Display u_7_segment_display_2 (
    .g(blackbox_1_output[23]), .f(blackbox_1_output[22]), .a(blackbox_1_output[21]),
    .b(blackbox_1_output[20]), .e(blackbox_1_output[19]), .d(blackbox_1_output[18]),
    .c(blackbox_1_output[17]), .dp(blackbox_1_output[16]));
  blackbox blackbox_1 (.ROM({multiplexer_1_out, multiplexer_2_out}), .Input(Input), .Output(blackbox_1_output));
  _7_Segment_Display u_7_segment_display_3 (
    .g(blackbox_1_output[15]), .f(blackbox_1_output[14]), .a(blackbox_1_output[13]),
    .b(blackbox_1_output[12]), .e(blackbox_1_output[11]), .d(blackbox_1_output[10]),
    .c(blackbox_1_output[9]), .dp(blackbox_1_output[8]));
  Multiplexer #(.select(3), .width(16)) multiplexer_2 (
    .in0(rom_1_data[31:16]), .in1(rom_1_data[15:0]), .in2(rom_1_data[15:0]), .in3(rom_1_data[31:16]),
    .in4(rom_1_data[15:0]), .in5(rom_2_data[15:0]), .in6(rom_2_data[15:0]), .in7(rom_1_data[15:0]),
    .out(multiplexer_2_out), .sel(counter_1_q));  // open: en
  _7_Segment_Display u_7_segment_display_4 (
    .g(blackbox_1_output[7]), .f(blackbox_1_output[6]), .a(blackbox_1_output[5]), .b(blackbox_1_output[4]),
    .e(blackbox_1_output[3]), .d(blackbox_1_output[2]), .c(blackbox_1_output[1]), .dp(blackbox_1_output[0]));

  // Notes on the sheet:
  //   contents of rom_1 (hex, n*v repeats v):
  //   45de459c 3db7a9ba abb7b7ae a7b449ae
  //   contents of rom_2 (hex, n*v repeats v):
  //   c9bd6b8b ef13cb56 bdfbb9da c96d31fb
  //   gauche
  //   droite
  //   <- une blackbox que vous pouvez ouvrir en double cliquant avec l'outil poke (ctrl+1)
endmodule

module blackbox (
  input  [31:0] ROM,
  input  [31:0] Input,
  output [31:0] Output
);

  wire [31:0] nand_1_out, nand_2_out, nand_3_out, nand_4_out, nand_5_out, nand_6_out, nand_7_out, nand_8_out,
       nand_9_out, nand_10_out, nand_11_out, nand_12_out, nand_13_out, nand_14_out;

  assign nand_1_out = ~(ROM & ROM);  // NAND_Gate nand_1, 32 bits wide
  assign nand_2_out = ~(Input & Input);  // NAND_Gate nand_2, 32 bits wide
  assign nand_3_out = ~(nand_1_out & nand_2_out);  // NAND_Gate nand_3, 32 bits wide
  assign nand_4_out = ~(ROM & Input);  // NAND_Gate nand_4, 32 bits wide
  assign nand_5_out = ~(nand_3_out & nand_4_out);  // NAND_Gate nand_5, 32 bits wide
  assign nand_6_out = ~(nand_5_out & nand_5_out);  // NAND_Gate nand_6, 32 bits wide
  assign nand_7_out = ~(Input & Input);  // NAND_Gate nand_7, 32 bits wide
  assign nand_8_out = ~(nand_6_out & nand_7_out);  // NAND_Gate nand_8, 32 bits wide
  assign nand_9_out = ~(nand_5_out & Input);  // NAND_Gate nand_9, 32 bits wide
  assign nand_10_out = ~(nand_8_out & nand_9_out);  // NAND_Gate nand_10, 32 bits wide
  assign nand_11_out = ~(nand_10_out & nand_10_out);  // NAND_Gate nand_11, 32 bits wide
  assign nand_12_out = ~(Input & Input);  // NAND_Gate nand_12, 32 bits wide
  assign nand_13_out = ~(nand_11_out & nand_12_out);  // NAND_Gate nand_13, 32 bits wide
  assign nand_14_out = ~(nand_10_out & Input);  // NAND_Gate nand_14, 32 bits wide
  assign Output = ~(nand_13_out & nand_14_out);  // NAND_Gate nand_15, 32 bits wide

  // Notes on the sheet:
  //   Toutes les portes peuvent être faites avec des NAND...
  //   ... et certaines portes sont involutives.
endmodule
